# Fritzing sketch Fritzing_Layout (saved by Fritzing 0.9.9b)
perfboards: 1

parts:
  MIDI_Out = DIN-5 jack (MIDI) [package=THT]
  MIDI_In = DIN-5 jack (MIDI) [package=THT]
  R2 = Resistor [tolerance=±5% power=0.25 resistance=220 package=THT]
  4N35_Optocoupler = IC, DIP package, 6 pins [chip_label=IC]
  R4 = Resistor [tolerance=±5% power=0.25 resistance=220 package=THT]
  R1 = Resistor [tolerance=±5% power=0.25 resistance=220 package=THT]
  R5 = Resistor [tolerance=±5% power=0.25 resistance=560 package=THT]
  J1_ESP32 = double row female pin header, 20 pins [form="♀ (female)"]
  J2_ESP32 = double row female pin header, 20 pins [form="♀ (female)"]
  7404_Hex_Inverter = IC, DIP package, 14 pins [chip_label=IC]
  D1 = Rectifier Diode [part_number=1N914 package="300 mil [THT]"]

nets:
  N1: MIDI_Out.5, R2.Pin_1
  N2: MIDI_Out.4, R1.Pin_0
  N3: MIDI_In.5, R4.Pin_1
  N4: MIDI_In.4, 4N35_Optocoupler.pin1, D1.cathode
  5V: R2.Pin_0, R5.Pin_0, J1_ESP32.pin1, 7404_Hex_Inverter.pin14
  N5: 4N35_Optocoupler.pin2, R4.Pin_0, D1.anode
  GND: 4N35_Optocoupler.pin4, J2_ESP32.pin19, 7404_Hex_Inverter.pin7
  N6: 4N35_Optocoupler.pin5, R5.Pin_1, J2_ESP32.pin8
  N7: R1.Pin_1, 7404_Hex_Inverter.pin4
  N8: J2_ESP32.pin9, 7404_Hex_Inverter.pin1
  N9: 7404_Hex_Inverter.pin2, 7404_Hex_Inverter.pin3
